# Fritzing sketch OledPCB (saved by Fritzing 0.9.3b)
circuit board: 4.57852cm x 5.10204cm
circuit board: 4.55971cm x 4.72574cm
circuit board: 3.54cm x 3.35cm
circuit board: 3.54cm x 3.35cm
circuit board: 4.32922cm x 4.95388cm
circuit board: 4.00937cm x 4.70222cm
breadboards: 1

parts:
  J3 = male pin header, 4 pins [form="♂ (male)"]
  Part5 = Arduino Nano (Rev3.0)
  Part6 = NRF24L01+ Breakout Board
  J4 = male pin header, 4 pins [form="♂ (male)"]
  Part7 = Arduino Nano (Rev3.0)
  Part8 = NRF24L01+ Breakout Board
  J5 = male pin header, 4 pins [form="♂ (male)"]
  Part9 = Arduino Nano (Rev3.0)
  Part10 = NRF24L01+ Breakout Board
  J6 = male pin header, 4 pins [form="♂ (male)"]
  Part11 = Arduino Nano (Rev3.0)
  Part12 = NRF24L01+ Breakout Board
  J7 = male pin header, 4 pins [form="♂ (male)"]
  Part13 = Arduino Nano (Rev3.0)
  Part14 = NRF24L01+ Breakout Board
  J8 = male pin header, 4 pins [form="♂ (male)"]
  Part15 = Arduino Nano (Rev3.0)
  Part16 = NRF24L01+ Breakout Board

nets:
  N1: J3.pin1, Part5.A4
  N2: J3.pin2, Part5.A5
  N3: J3.pin3, Part5.5V
  GND: J3.pin4, Part5.GND, Part6.GND
  N4: Part5.D7, Part6.CE
  N5: Part5.D8, Part6.CS
  N6: Part5.D11/MOSI, Part6.MOSI
  N7: Part5.D12/MISO, Part6.MISO
  3V3: Part5.3V3, Part6.VCC
  N8: Part5.D13/SCK, Part6.SCK
  N9: J4.pin1, Part7.A4
  N10: J4.pin2, Part7.A5
  N11: J4.pin3, Part7.5V
  GND_2: J4.pin4, Part7.GND, Part8.GND
  N12: Part7.D7, Part8.CE
  N13: Part7.D8, Part8.CS
  N14: Part7.D11/MOSI, Part8.MOSI
  N15: Part7.D12/MISO, Part8.MISO
  3V3_2: Part7.3V3, Part8.VCC
  N16: Part7.D13/SCK, Part8.SCK
  N17: J5.pin1, Part9.A4
  N18: J5.pin2, Part9.A5
  N19: J5.pin3, Part9.5V
  GND_3: J5.pin4, Part9.GND, Part10.GND
  N20: Part9.D7, Part10.CE
  N21: Part9.D8, Part10.CS
  N22: Part9.D11/MOSI, Part10.MOSI
  N23: Part9.D12/MISO, Part10.MISO
  3V3_3: Part9.3V3, Part10.VCC
  N24: Part9.D13/SCK, Part10.SCK
  N25: J6.pin1, Part11.A4
  N26: J6.pin2, Part11.A5
  N27: J6.pin3, Part11.5V
  GND_4: J6.pin4, Part11.GND, Part12.GND
  N28: Part11.D6, Part12.CS
  N29: Part11.D7, Part12.CE
  N30: Part11.D11/MOSI, Part12.MISO
  N31: Part11.D12/MISO, Part12.MOSI
  N32: Part11.D13/SCK, Part12.SCK
  N33: J7.pin1, Part13.A4
  N34: J7.pin2, Part13.A5
  N35: J7.pin3, Part13.5V
  GND_5: J7.pin4, Part13.GND, Part14.GND
  N36: Part13.D7, Part14.CE
  N37: Part13.D8, Part14.CS
  N38: Part13.D11/MOSI, Part14.MOSI
  N39: Part13.D12/MISO, Part14.MISO
  3V3_4: Part13.3V3, Part14.VCC
  N40: Part13.D13/SCK, Part14.SCK
  N41: J8.pin1, Part15.A4
  N42: J8.pin2, Part15.A5
  N43: J8.pin3, Part15.5V
  GND_6: J8.pin4, Part15.GND, Part16.GND
  N44: Part15.D7, Part16.CE
  N45: Part15.D8, Part16.CS
  N46: Part15.D11/MOSI, Part16.MOSI
  N47: Part15.D12/MISO, Part16.MISO
  3V3_5: Part15.3V3, Part16.VCC
  N48: Part15.D13/SCK, Part16.SCK

notes:
  Top
  5V
  GND
  Vin
